// Logisim project ALU74181.circ as structural Verilog: 1 circuit, main circuit main
module main (
  input  in_1,
  input  B3,
  input  A3,
  input  B2,
  input  A2,
  input  B1,
  input  A1,
  input  B0,
  input  A0
);

  wire and_1_out, and_2_out, and_3_out, and_4_out, and_5_out, and_6_out, and_7_out, and_8_out, and_9_out,
       and_10_out, and_11_out, and_12_out, and_13_out, and_14_out, and_15_out, and_16_out, and_17_out,
       and_18_out, and_19_out, and_20_out, and_21_out, and_22_out, and_23_out, and_24_out, and_25_out,
       nand_1_out, nor_1_out, nor_2_out, nor_9_out, not_1_out, not_2_out, not_3_out, not_4_out, not_5_out,
       not_6_out, not_7_out, or_1_out, undriven, undriven_2, undriven_3, undriven_4, undriven_5, undriven_6;

  LED led_1 ();  // open: in
  LED led_2 ();  // open: in
  LED led_3 ();  // open: in
  LED led_4 ();  // open: in
  not not_1 (not_1_out, B3);
  not not_2 (not_2_out, B2);
  not not_3 (not_3_out, B1);
  not not_4 (not_4_out, B0);
  not not_5 (not_5_out, in_1);
  LED led_5 (.in(not_5_out));
  and and_1 (and_1_out, B3, undriven_4, A3);
  and and_2 (and_2_out, A3, undriven_3, not_1_out);
  and and_3 (and_3_out, not_1_out, undriven_2);
  and and_4 (and_4_out, undriven, B3);
  buf and_5 (and_5_out, A3);  // AND_Gate
  and and_6 (and_6_out, B2, undriven_4, A2);
  and and_7 (and_7_out, A2, undriven_3, not_2_out);
  and and_8 (and_8_out, not_2_out, undriven_2);
  and and_9 (and_9_out, undriven, B2);
  buf and_10 (and_10_out, A2);  // AND_Gate
  and and_11 (and_11_out, B1, undriven_4, A1);
  and and_12 (and_12_out, A1, undriven_3, not_3_out);
  and and_13 (and_13_out, not_3_out, undriven_2);
  and and_14 (and_14_out, undriven, B1);
  buf and_15 (and_15_out, A1);  // AND_Gate
  and and_16 (and_16_out, B0, undriven_4, A0);
  and and_17 (and_17_out, A0, undriven_3, not_4_out);
  and and_18 (and_18_out, not_4_out, undriven_2);
  and and_19 (and_19_out, undriven, B0);
  buf and_20 (and_20_out, A0);  // AND_Gate
  LED led_6 (.in(undriven_5));
  LED led_7 (.in(nor_1_out));
  nor nor_1 (nor_1_out, and_1_out, and_2_out);
  LED led_8 (.in(nor_2_out));
  nor nor_2 (nor_2_out, and_3_out, and_4_out, and_5_out);
  // NOR_Gate nor_3 has open pins: in1=and_6_out, in3=and_7_out, out=open
  // NOR_Gate nor_4 has open pins: in0=and_8_out, in2=and_9_out, in4=and_10_out, out=open
  // NOR_Gate nor_5 has open pins: in1=and_11_out, in3=and_12_out, out=open
  // NOR_Gate nor_6 has open pins: in0=and_13_out, in2=and_14_out, in4=and_15_out, out=open
  // NOR_Gate nor_7 has open pins: in1=and_16_out, in3=and_17_out, out=open
  // NOR_Gate nor_8 has open pins: in0=and_18_out, in2=and_19_out, in4=and_20_out, out=open
  buf and_21 (and_21_out, nor_2_out);  // AND_Gate
  and and_22 (and_22_out, nor_1_out, undriven_6);
  buf and_23 (and_23_out, nor_1_out);  // AND_Gate
  buf and_24 (and_24_out, nor_1_out);  // AND_Gate
  // AND_Gate and_25 has open pins: out=and_25_out
  // NAND_Gate nand_1 has open pins: out=nand_1_out
  nor nor_9 (nor_9_out, and_21_out, and_22_out, and_23_out, and_24_out);
  not not_6 (not_6_out, nor_2_out);
  not not_7 (not_7_out, nor_9_out);
  or or_1 (or_1_out, not_7_out, and_25_out);
  // AND_Gate and_26 has open pins: in1=undriven_6, in3=not_6_out, out=open
  LED led_9 (.in(nor_9_out));
  LED led_10 (.in(or_1_out));
  LED led_11 (.in(nand_1_out));

  // Notes on the sheet:
  //   S1
  //   S0
  //   S3
  //   S2
  //   why is there a random ahhh and gate here
  //   G
  //   all technically notted but idrgaf
endmodule
